# Fritzing sketch Projet SmartPatate (saved by Fritzing 0.9.3b)
breadboards: 1

parts:
  Composant1 = Arduino Uno (Rev3)
  R1 = Resistor [tolerance=±5% resistance=10k package=THT]
  R2 = Resistor [tolerance=±5% resistance=1M package=THT]
  C1 = Ceramic Capacitor [capacitance=10nF package="100 mil [THT, multilayer]"]
  D1 = Rectifier Diode [part_number=1N4548 package="300 mil [THT]"]
  C2 = Ceramic Capacitor [capacitance=0.1nF package="100 mil [THT, multilayer]"]
  R3 = Resistor [tolerance=±5% resistance=3.3 package=THT]
  R4 = Basic Flex Resistor
  LED1 = LED - 5mm [color="Red (633nm)" package="5 mm [THT]"]
  LED2 = LED - 5mm [color="Green (570nm)" package="5 mm [THT]"]
  J1 = Piezo Speaker
  L1 = Inductor [inductance=10H package="0603 [SMD]"]
  L1_2 = Inductor [inductance=10mH package="1206 [SMD]"]

nets:
  N1: Composant1.A0, C2.1
  N2: Composant1.D9_PWM, R1.Pin_1
  GND: Composant1.GND, R2.Pin_1, C2.0, R3.Pin_0, LED1.cathode, J1.pin1
  N3: Composant1.D4, LED2.anode
  N4: Composant1.D5_PWM, LED1.anode
  N5: R1.Pin_0, R3.Pin_1, L1.pin_1, L1_2.pin_1
  N6: R2.Pin_0, D1.cathode
  N7: C1.0, D1.anode, L1.pin_0, L1_2.pin_0
  N8: C1.1, R4.pin_1
  N9: LED2.cathode, J1.pin2

notes:
  Electrode
  = Patate
